# Fritzing sketch RRFTracker (saved by Fritzing 0.9.3b)
breadboards: 1

parts:
  U1 = NodeMCU V3.0
  Part1 = LCD1602-I2C
  R1 = Resistor [tolerance=±5% resistance=330 package=THT]
  R2 = Resistor [tolerance=±5% resistance=330 package=THT]
  R3 = Resistor [tolerance=±5% resistance=330 package=THT]
  LED1 = LED - 3mm [color="Blue (430nm)" package="3 mm [THT]"]
  LED2 = LED - 3mm [color="Red (633nm)" package="3 mm [THT]"]
  LED3 = LED - 3mm [color="Green (555nm)" package="3 mm [THT]"]

nets:
  N1: U1.D1, Part1.SCL
  N2: U1.D2, Part1.SDA
  N3: U1.D4, R1.Pin_0
  GND: U1.GND, Part1.GND, LED1.cathode, LED2.cathode, LED3.cathode
  N4: U1.D5, R2.Pin_0
  N5: U1.D8, R3.Pin_0
  VIN: U1.Vin, Part1.VCC
  N6: R1.Pin_1, LED1.anode
  N7: R2.Pin_1, LED2.anode
  N8: R3.Pin_1, LED3.anode

notes:
  RRFTracker V0.1 - F4HWN Armel

custom parts:
  NodeMCU V3.0: ESP8266 based NodeMCU
  LCD1602-I2C: A standard character display, usually with 2x16 characters. Comes in many colors with LCM1602 IIC attached.

// code stored in the sketch: NodemcuTemperatureRelayLcd.ino
/********************** LYBRARY ****************************/

#define BLYNK_PRINT Serial // Comment this out to disable prints and save space


#include <ESP8266WiFi.h>
#include <BlynkSimpleEsp8266.h>
#include <OneWire.h>
#include <DallasTemperature.h>
#include <LiquidCrystal_I2C.h>

/* TIMER */
#include <SimpleTimer.h>
SimpleTimer timer;

/********************** BLYNK ACCOUNT ****************************/
char auth[] = "BLYNK_TOKEN";
char ssid[] = "SSID";
char pass[] = "PASS";


/********************** HARDWARE ****************************/
// Temperature sensor full ID, including family code and CRC
// use OneWire Scanner to get the address
DeviceAddress tempSensor = { 0x28, 0xFF, 0x64, 0x1D, 0x8F, 0x87, 0x95, 0xB1 };

// Pin used for the OneWire interface
#define ONE_WIRE_BUS 14 //pin D5 nodemcu Lolin v3

LiquidCrystal_I2C lcd(0x27, 16, 2); //LCD address and type.
//D2 = SDA D1 = SCL

/**************BIG CHAR*********************************************/


/********************** TEMPERATURE DEF****************************/
OneWire oneWire(ONE_WIRE_BUS);
DallasTemperature DS18B20(&oneWire);
float temp;

/********************** SETUP ****************************/
void setup()
{
  // Debug console
  Serial.begin(9600);
  Blynk.begin(auth, ssid, pass, IPAddress(188,166,206,43), 8080); //use other method to connect to blynk server
  DS18B20.begin();
  timer.setInterval(15000L, getSendData);
  Blynk.syncAll();

  pinMode(2, OUTPUT);
  
  lcd.init();
  lcd.backlight();
  lcd.clear();

}

/********************** LOOP ****************************/
void loop()
{
  Blynk.run();
  timer.run();
}

/********************** Send Sensor data to Blynk ****************************/
void getSendData()
{
  DS18B20.requestTemperatures(); 
  temp = DS18B20.getTempCByIndex(0);
  Serial.println(temp);
  Blynk.virtualWrite(10, temp); //virtual pin V10
  
  lcd.setCursor(0, 0);
  lcd.print("Temp:");
  lcd.setCursor(6,0);
  lcd.print(temp);
  lcd.setCursor(12,0);
  lcd.print("'C");
}
